// Logisim project RISC 32 BIT FETCH.circ as structural Verilog: 1 circuit, main circuit main
module main (
  input  [31:0] Instruction
);


  // Other names for the same wires on the sheet: First[7:0] = Instruction[7:0]; OP2[7:0] = Instruction[7:0];
  //   OP1[7:0] = Instruction[15:8]; Second[7:0] = Instruction[15:8]; Dest[7:0] = Instruction[23:16];
  //   Third[7:0] = Instruction[23:16]; Fourth[7:0] = Instruction[31:24]; Number[1:0] = Instruction[25:24];
  //   Instruction_t[2:0] = Instruction[28:26]; Type[2:0] = Instruction[31:29]
endmodule
