// Logisim project RISC 32 BIT MAIN.circ as structural Verilog: 1 circuit, main circuit main
module main (
  input  [31:0] in_1
);

  wire and_2_out, and_3_out, and_4_out, Arithmetic, Clock, clock_1_out, CLR, controlled_buffer_4_out, EnOP1,
       EnOP2, EnRC, HALT, LD, Logic, MOV, multiplexer_4_out, not_1_out, not_2_out, not_3_out, not_4_out,
       not_5_out, OneAddress, or_1_out, or_2_out, or_3_out, or_5_out, or_6_out, or_7_out, ThreeAddress,
       TwoAddress, ZeroAddress;
  wire [1:0] Num, SelectInput, SelectREG;
  wire [2:0] Instr, OPCODE;
  wire [4:0] REG1, REG2;
  wire [7:0] Dest;
  wire [15:0] Input;
  wire [31:0] Accumulator, controlled_buffer_1_out, controlled_buffer_3_out, controlled_buffer_5_out,
       controlled_buffer_6_out, main_1_p7, multiplexer_1_out, multiplexer_2_out, multiplexer_3_out, OP1, OP2,
       register_2_q, Result;

  Clock clock_1 (.out(clock_1_out));
  Multiplexer #(.width(32)) multiplexer_1 (
    .in0(OP1), .in1(Accumulator), .out(multiplexer_1_out), .sel(OneAddress), .en(1'b1));
  Multiplexer #(.width(32)) multiplexer_2 (.in0(OP2), .in1(OP1), .out(multiplexer_2_out), .sel(OneAddress), .en(1'b1));
  and and_1 (Clock, clock_1_out, ~HALT);  // AND_Gate
  assign controlled_buffer_1_out = OneAddress ? Result : 32'bz;  // Controlled_Buffer controlled_buffer_1
  // RISC_32_BIT_ALU_main main_1: pin names not known; wires that end beside it: multiplexer_1_out, multiplexer_2_out, OPCODE, Clock, Instr, MOV, main_1_p7
  Register #(.width(32)) u_Accumulator (
    .D(controlled_buffer_1_out), .en(OneAddress), .Q(Accumulator), .clk(Clock), .clr(and_2_out));
  and and_2 (and_2_out, ZeroAddress, CLR);
  RISC_32_BIT_DECODE_main main_2 (
    .Clock(Clock), .out_34(LD), .out_36(MOV), .out_37(CLR), .out_38(HALT), .out_39(Dest),
    .out_40(Input[15:8]), .out_41(Input[7:0]), .out_42(Num), .Instruction(in_1), .Arithmetic(Arithmetic),
    .Logic(Logic), .out_5(Instr), .out_6(OPCODE));  // open: out_3, out_4, out_7, out_8, out_9, out_10, out_11, out_12, out_13, out_14, out_15, out_16, out_17, out_18, out_19, out_20, out_21, out_22, out_23, out_24, out_25, out_26, out_32, out_33, out_35, BranchJump, RegInstr, Stack
  // Probe on main_1_p7
  and and_3 (and_3_out, or_1_out, not_1_out);
  or or_1 (or_1_out, Logic, Arithmetic);
  RISC_32_BIT_MEMORY_main main_3 (.in_3(Clock));  // open: in_1, in_2, in_4, in_5, in_6, out_7, out_8
  assign Result = and_3_out ? main_1_p7 : 32'bz;  // Controlled_Buffer controlled_buffer_2
  not not_1 (not_1_out, MOV);
  Register #(.width(32)) register_1 (.clk(Clock), .clr(1'b0));  // open: D, en, Q
  not not_2 (not_2_out, MOV);
  assign controlled_buffer_3_out = not_2_out ? Result : 32'bz;  // Controlled_Buffer controlled_buffer_3
  not not_3 (not_3_out, MOV);
  not not_4 (not_4_out, OneAddress);
  Multiplexer #(.select(2), .width(32)) multiplexer_3 (
    .in0(controlled_buffer_3_out), .in1(OP1), .in2({{16{1'b0}}, Input}), .out(multiplexer_3_out),
    .sel(SelectInput), .en(not_4_out));  // open: in3
  Multiplexer multiplexer_4 (.in0(1'b0), .in1(1'b1), .out(multiplexer_4_out), .sel(CLR), .en(1'b1));
  assign controlled_buffer_4_out = not_3_out ? EnOP1 : 1'bz;  // Controlled_Buffer controlled_buffer_4
  not not_5 (not_5_out, MOV);
  assign controlled_buffer_5_out = not_5_out ? multiplexer_3_out : 32'bz;  // Controlled_Buffer controlled_buffer_5
  Register #(.width(32)) register_2 (
    .D(controlled_buffer_5_out), .en(not_5_out), .Q(register_2_q), .clk(Clock), .clr(MOV));
  assign controlled_buffer_6_out = not_5_out ? register_2_q : 32'bz;  // Controlled_Buffer controlled_buffer_6
  Pull_Resistor pull_resistor_1 (.node(EnRC));
  Pull_Resistor pull_resistor_2 (.node(controlled_buffer_4_out));
  Pull_Resistor pull_resistor_3 (.node(EnOP2));
  // RISC_32_BIT_REGISTERS_main main_4: pin names not known; wires that end beside it: controlled_buffer_6_out, Dest[4:0], REG1, REG2, EnRC, multiplexer_4_out, controlled_buffer_4_out, EnOP2, MOV, Clock, OP1, OP2
  and and_4 (and_4_out, TwoAddress, ~MOV);  // AND_Gate
  and and_5 (ThreeAddress, Num[0], Num[1]);
  and and_6 (TwoAddress, ~Num[0], Num[1]);  // AND_Gate
  and and_7 (OneAddress, Num[0], ~Num[1]);  // AND_Gate
  and and_8 (ZeroAddress, ~Num[0], ~Num[1]);  // AND_Gate
  or or_2 (or_2_out, ThreeAddress, TwoAddress, OneAddress);
  or or_3 (or_3_out, ThreeAddress, MOV);
  or or_4 (EnRC, Arithmetic, Logic, MOV, LD);
  or or_5 (or_5_out, Arithmetic, Logic);
  Multiplexer #(.select(2), .width(5)) multiplexer_5 (
    .in0({5{1'b0}}), .in1({5{1'b0}}), .in2(Input[12:8]), .in3(Input[4:0]), .out(REG2), .sel(SelectREG),
    .en(1'b1));
  or or_6 (or_6_out, ThreeAddress, TwoAddress);
  or or_7 (or_7_out, or_2_out, MOV);
  Priority_Encoder #(.select(2)) priority_encoder_1 (
    .in1(OneAddress), .in2(and_4_out), .in3(or_3_out), .out(SelectREG));  // open: in0, gs, en_out, en_in
  Priority_Encoder #(.select(2)) priority_encoder_2 (
    .in0(or_5_out), .in1(MOV), .in2(LD), .out(SelectInput));  // open: in3, gs, en_out, en_in
  and and_9 (EnOP2, or_6_out, ~ZeroAddress, ~MOV, ~LD);  // AND_Gate
  and and_10 (EnOP1, or_7_out, ~ZeroAddress, ~LD, ~CLR);  // AND_Gate
  Multiplexer #(.select(2), .width(5)) multiplexer_6 (
    .in1(Dest[4:0]), .in2(Dest[4:0]), .in3(Input[12:8]), .out(REG1), .sel(SelectREG), .en(1'b1));  // open: in0

  // Other names for the same wires on the sheet: RC[4:0] = Dest[4:0]; O2[7:0] = Input[7:0]; O1[7:0] = Input[15:8]
endmodule
